# Fritzing sketch smart patate (saved by Fritzing 0.9.3b)
breadboards: 1

parts:
  Arduino = Arduino Uno (Rev3)
  R3 = Resistor [tolerance=±5% resistance=1M package=THT]
  D1 = Rectifier Diode [part_number=1N4148 package="300 mil [THT]"]
  C2 = Ceramic Capacitor [capacitance=10nF package="100 mil [THT, multilayer]"]
  L1 = Inductor [part_number="10 mH" package="400 mil [THT]"]
  R4 = Resistor [tolerance=±5% resistance=220 package=THT]
  LED2 = LED - 5mm [color="Green (565nm)" package="5 mm [THT]"]
  LED3 = LED - 5mm [color="Red (633nm)" package="5 mm [THT]"]
  LED1 = smd LED [color="Orange (620nm)" package="0603 [SMD]"]
  C1 = Ceramic Capacitor [capacitance=0.1nF package="100 mil [THT, multilayer]"]

nets:
  N1: Arduino.A0, R3.Pin_0, D1.cathode, C1.0
  N2: Arduino.D9_PWM, L1.pin_1
  N3: Arduino.GND, R3.Pin_1, R4.Pin_1, C1.1
  N4: Arduino.D2, LED3.anode
  N5: Arduino.D3_PWM, LED1.anode
  N6: Arduino.D4, LED2.anode
  N7: D1.anode, C2.1, L1.pin_0
  N8: R4.Pin_0, LED2.cathode, LED3.cathode, LED1.cathode
